# Fritzing sketch Hardware Connection (saved by Fritzing 0.9.3b)
breadboards: 1

parts:
  Raspberry_Pi_1 = Raspberry Pi 3 [part_number=RPI-3-V1.2]
  M1 = NEO-7M GPS Module [part_number=GY-GPSV3-NEO]
  M2 = BME680 Module [part_number=CJMCU-680]
  A1 = PMS5003
  MOTOR1 = Vibration Motor
  BAT1 = BC9VPC [package=bc9vpc]
  IC1 = Single-Chip USB to UART Bridge [package=mlp28]
  LED2 = LEDs [package=led10mm]
  R1 = Resistor [tolerance=±5% resistance=220 package="0603 [SMD]"]
  J1 = Piezo Speaker  # not connected

nets:
  N1: Raspberry_Pi_1.GPIO2, M2.SDA
  N2: Raspberry_Pi_1.GPIO3, M2.SCL
  N3: Raspberry_Pi_1.GIPO24, MOTOR1.POS
  N4: Raspberry_Pi_1.GIPO23, LED2.A
  N5: Raspberry_Pi_1.GIPO15, M1.Tx
  N6: Raspberry_Pi_1.GIPO14, M1.Rx
  N7: Raspberry_Pi_1.GND, MOTOR1.NEG
  GND: M1.GND, M2.GND, A1.Pin_8, BAT1.V-
  VCC: M1.Vcc, M2.VCC, A1.Pin_7, BAT1.V+
  N8: A1.Pin_3, IC1.TXD
  N9: A1.Pin_4, IC1.RXD
  N10: LED2.C, R1.Pin_1

notes:
  Air530
  BME680
  PMS7003
  Power Bank
  Vibrating Motor Disc
  USB TO UART Converter
  PI 400
  BreadBoard
  LED
  Resistor
  PIR BUZZER

custom parts:
  NEO-7M GPS Module: GY-GPSV3-NEO NEO-7M GPS Module Module based on U-blox NEO-7M GPS engine, incorporating regulator for 3.3-5V DC input, MS621FE-compatible rechargeable battery for backup and EEPROM for storing configuration settings. Links: NEO-7 series product information page NEO-7 Datasheet
  BME680 Module: Bosch BME680 Development Module The BME680 is a digital 4-in-1 sensor that measures air quality [gas], humidity, pressure and temperature. Links: BME680 product datasheet
  PMS5003: PMS5003 is a kind of digital and universal particle concentration sensor, which can be used to obtain the number of suspended particles in the air.
  Vibration Motor: An eccentric vibration motor!
